// Logisim project Proj.circ as structural Verilog: 1 circuit, main circuit main
module main (
);

  wire _0, _1, _2, _3, _4, _5, _6, _7, _8, _9, or_5_out;
  wire [3:0] or_1_out, register_1_q, rom_1_data;

  Button u__1 (.out(_1));
  Button u__4 (.out(_4));
  Button u__7 (.out(_7));
  Button u__2 (.out(_2));
  Button u__3 (.out(_3));
  Button u__6 (.out(_6));
  Button u__5 (.out(_5));
  Button u__9 (.out(_9));
  Button u__8 (.out(_8));
  Button u__0 (.out(_0));
  or or_1 (or_1_out[0], _1, _3, _5, _7, _9);
  or or_2 (or_1_out[1], _2, _3, _6, _7);
  or or_3 (or_1_out[2], _4, _5, _6, _7);
  or or_4 (or_1_out[3], _8, _9);
  or or_5 (or_5_out, _0, or_1_out[0], or_1_out[1], or_1_out[2], or_1_out[3]);
  Hex_Digit_Display hex_digit_display_1 (.value(register_1_q));  // open: dp
  Register #(.width(4), .trigger("high")) register_1 (
    .D(rom_1_data), .Q(register_1_q), .clk(or_5_out));  // open: en, clr
  ROM #(.addrWidth(4), .dataWidth(4)) rom_1 (.addr(or_1_out), .data(rom_1_data));  // open: sel

  // Notes on the sheet:
  //   contents of rom_1 (hex, n*v repeats v):
  //   0 1 2 3 4 5 6 7 8 9 a b c d e f
endmodule
